# Fritzing sketch electrtical_sketch (saved by Fritzing 0.9.3b)
breadboards: 1

parts:
  Bauteil1 = Arduino Uno (Rev3)
  J1 = Basic Servo
  J2 = Basic Servo
  S1 = Pushbutton [package=THT]
  S2 = Pushbutton [package=THT]
  U1 = POT [package=pot_alpha_rv16af-20]
  U2 = POT [package=pot_alpha_rv16af-20]
  U3 = POT [package=pot_alpha_rv16af-20]
  U4 = POT [package=pot_alpha_rv16af-20]
  LED1 = LED - 3mm [color="Red (633nm)" package="3 mm [THT]"]

nets:
  N1: Bauteil1.A0, U1.S
  N2: Bauteil1.A1, U2.S
  N3: Bauteil1.A2, U3.S
  N4: Bauteil1.A3, U4.S
  N5: Bauteil1.D8, J2.pulse
  N6: Bauteil1.D9_PWM, J1.pulse
  N7: Bauteil1.D10_PWM/SS, S1.leg0
  N8: Bauteil1.D11_PWM/MOSI, S2.leg0
  N9: Bauteil1.D12/MISO, LED1.anode
  VCC: Bauteil1.5V, J1.vcc, J2.vcc, U1.A, U2.A, U3.A, U4.A
  GND: Bauteil1.GND, J1.gnd, J2.gnd, S1.leg1, S2.leg1, U1.E, U2.E, U3.E, U4.E, LED1.cathode
